# Fritzing sketch TempControlLayout (saved by Fritzing 0.9.1b)
perfboards: 1

parts:
  Bauteil1 = Arduino Uno (Rev3)
  HC = DHT11 Humitidy and Temperature Sensor
  W = DHT11 Humitidy and Temperature Sensor
  Tiny_RTC = Tiny RTC
  Wifi = ESP8266 WiFi Module [part_number=ESP8266]
  C1 = Electrolytic Capacitor [capacitance=220µF package="100 mil [THT, electrolytic]"]
  R1 = Resistor [tolerance=±20% resistance=1k package=THT]
  R2 = Resistor [tolerance=±5% resistance=1.5k package=THT]

nets:
  N1: Bauteil1.A4/SDA, Tiny_RTC.SDA
  N2: Bauteil1.A5/SCL, Tiny_RTC.SCL
  GND: Bauteil1.GND, HC.GND
  N3: Bauteil1.D0/RX, Wifi.TXD
  N4: Bauteil1.D1/TX, R1.Pin_0
  N5: Bauteil1.D2, W.DATA
  N6: Bauteil1.D4, HC.DATA
  VDD: Bauteil1.5V, HC.VDD, W.VDD, Tiny_RTC.VCC
  GND_2: W.GND, Wifi.GND
  N7: Wifi.RXD, R1.Pin_1, R2.Pin_1
  N8: C1.+, R2.Pin_0

custom parts:
  DHT11 Humitidy and Temperature Sensor: DHT11 Humidity and Temperature Sensor
  Tiny RTC: Tiny RTC I2C module DS1370Z RTC and AT24C32 EEPROM
  ESP8266 WiFi Module: Generic WiFi Module based on the ESP8266 with onboard PCB antenna and UART communications
